# Fritzing sketch project-luna (saved by Fritzing 0.9.3b)
perfboards: 2

parts:
  LiPo_S2_(7_4V) = DC Power [voltage=7.4V frequency=60]
  J5 = female pin header, 10 pins [form="♀ (female)"]
  J6 = female pin header, 2 pins [form="♀ (female)"]
  M1 = Adafruit TB6612 DC and Stepper Motor Driver [part_number="Adafruit #2448"]
  M2 = Adafruit TB6612 DC and Stepper Motor Driver [part_number="Adafruit #2448"]
  M_A2 = Screw terminal - 2 pins [package=THT]
  M_A1 = Screw terminal - 2 pins [package=THT]
  A_B1 = Screw terminal - 2 pins [package=THT]
  J4 = female pin header, 2 pins [form="♀ (female)"]
  J7 = female pin header, 2 pins [form="♀ (female)"]
  Particle_Photon1 = Photon
  J9 = male pin header, 10 pins [form="♂ (male)"]
  J10 = male pin header, 2 pins [form="♂ (male)"]
  J3 = male pin header, 2 pins [form="♂ (male)"]
  J11 = male pin header, 2 pins [form="♂ (male)"]
  8-Bit_Shift_Register = 74HC595 [package="DIP16 [THT]"]
  M_B2 = Screw terminal - 2 pins [package=THT]

nets:
  N1: LiPo_S2_(7_4V).V+, J6.pin1, M1.Vmotor, M1.PWRIN, M2.Vmotor, M2.PWRIN, J7.pin1, Particle_Photon1.VIN, J10.pin2, J11.pin2
  GND: LiPo_S2_(7_4V).V-, J6.pin2, M1.GND, M2.GND, J4.pin2, J7.pin2, Particle_Photon1.GND, J10.pin1, J3.pin1, J11.pin1, 8-Bit_Shift_Register.GND, 8-Bit_Shift_Register.OE
  N2: J5.pin1, M1.AIN1, J9.pin1, 8-Bit_Shift_Register.Q0
  N3: J5.pin2, M1.AIN2, J9.pin2, 8-Bit_Shift_Register.Q1
  N4: J5.pin3, M1.BIN1, J9.pin3, 8-Bit_Shift_Register.Q2
  N5: J5.pin4, M1.BIN2, J9.pin4, 8-Bit_Shift_Register.Q3
  N6: J5.pin5, M2.AIN1, J9.pin5, 8-Bit_Shift_Register.Q4
  N7: J5.pin6, M2.AIN2, J9.pin6, 8-Bit_Shift_Register.Q5
  N8: J5.pin7, M2.BIN1, J9.pin7, 8-Bit_Shift_Register.Q6
  N9: J5.pin8, M2.BIN2, J9.pin8, 8-Bit_Shift_Register.Q7
  N10: J5.pin9, M1.PWMB, M1.PWMA, Particle_Photon1.D0, J9.pin9
  N11: J5.pin10, M2.PWMB, M2.PWMA, Particle_Photon1.D1, J9.pin10
  VCC: M1.VCC, M2.VCC, J4.pin1, Particle_Photon1.3V3, J3.pin2, 8-Bit_Shift_Register.VCC
  N12: M1.MOTORA1, M_A1.pin1
  N13: M1.MOTORA2, M_A1.pin2
  N14: M1.MOTORB2, A_B1.pin1
  N15: M1.MOTORB1, A_B1.pin2
  N16: M2.MOTORA1, M_A2.pin1
  N17: M2.MOTORA2, M_A2.pin2
  N18: M2.MOTORB2, M_B2.pin1
  N19: M2.MOTORB1, M_B2.pin2
  N20: Particle_Photon1.D2, 8-Bit_Shift_Register.DS
  N21: Particle_Photon1.D4, 8-Bit_Shift_Register.ST_CP
  N22: Particle_Photon1.D5, 8-Bit_Shift_Register.SH_CP
  N23: Particle_Photon1.D6, 8-Bit_Shift_Register.MR

notes:
  LiPo 7,4V
  Particle Power Shield
  (connect to 7-20V Input)

custom parts:
  Adafruit TB6612 DC and Stepper Motor Driver: Spin two DC motors, step one bi-polar or uni-polar stepper, or fire off two solenoids with 1.2A per channel using the TB6612. These are perhaps better known as "the drivers in our assembled Adafruit Motorshield or Motor HAT." We really like these dual H-bridges, so if you want to control motors without a shield or HAT these are easy to include on any solderless breadboard or perma-proto.
